// Logisim project circuit.circ as structural Verilog
// NOT
module _74HC04 (
  input  _1A,
  input  Vcc,
  input  _6A,
  input  _2A,
  input  _5A,
  input  _3A,
  input  _4A,
  input  GND,
  output _1Y,
  output _6Y,
  output _2Y,
  output _5Y,
  output _3Y,
  output _4Y
);

  not not_1 (_1Y, _1A);
  not not_2 (_2Y, _2A);
  not not_3 (_3Y, _3A);
  not not_4 (_6Y, _6A);
  not not_5 (_5Y, _5A);
  not not_6 (_4Y, _4A);
endmodule

// AND
module _74HC08 (
  input  _1A,
  input  Vcc,
  input  _1B,
  input  _4A,
  input  _4B,
  input  _2A,
  input  _2B,
  input  _3A,
  input  _3B,
  input  GND,
  output _1Y,
  output _4Y,
  output _2Y,
  output _3Y
);

  and and_1 (_1Y, _1B, _1A);
  and and_2 (_4Y, _4A, _4B);
  and and_3 (_2Y, _2B, _2A);
  and and_4 (_3Y, _3A, _3B);
endmodule

// OR
module _74HC32 (
  input  _1A,
  input  Vcc,
  input  _1B,
  input  _4A,
  input  _4B,
  input  _2A,
  input  _2B,
  input  _3A,
  input  _3B,
  input  GND,
  output _1Y,
  output _4Y,
  output _2Y,
  output _3Y
);

  or or_1 (_1Y, _1B, _1A);
  or or_2 (_4Y, _4A, _4B);
  or or_3 (_2Y, _2B, _2A);
  or or_4 (_3Y, _3A, _3B);
endmodule

// NAND
module _74HC00 (
  input  _1A,
  input  Vcc,
  input  _1B,
  input  _4A,
  input  _4B,
  input  _2A,
  input  _2B,
  input  _3A,
  input  _3B,
  input  GND,
  output _1Y,
  output _4Y,
  output _2Y,
  output _3Y
);

  nand nand_1 (_1Y, _1B, _1A);
  nand nand_2 (_4Y, _4A, _4B);
  nand nand_3 (_2Y, _2B, _2A);
  nand nand_4 (_3Y, _3A, _3B);
endmodule

module Decoder (
  input  op0,
  input  op1,
  input  op2,
  input  op3,
  input  C_Flag,
  output SELECT_B,
  output SELECT_A,
  output LOAD_0,
  output LOAD_1,
  output LOAD_2,
  output LOAD_3
);

  wire n74hc10_1__3y, n74hc32_1__4y, not_1_out;

  not not_1 (not_1_out, C_Flag);
  _74HC32 u_74hc32_1 (
    ._1A(op2), ._1B(op3), ._1Y(LOAD_0), ._2A(op0), ._2B(op3), ._2Y(SELECT_A), ._4A(not_1_out), ._4B(op0),
    ._4Y(n74hc32_1__4y), ._3A(n74hc10_1__3y), ._3B(op3), ._3Y(LOAD_1));  // open: GND, Vcc
  _74HC10 u_74hc10_1 (
    ._1A(op3), ._1B(n74hc10_1__3y), ._2A(n74hc32_1__4y), ._2B(op2), ._2C(op3), ._2Y(LOAD_3), ._1C(1'b1),
    ._1Y(LOAD_2), ._3C(1'b1), ._3B(1'b1), ._3A(op2), ._3Y(n74hc10_1__3y));  // open: GND, Vcc

  assign SELECT_B = op1;
endmodule

// NAND_3
module _74HC10 (
  input  _1A,
  input  Vcc,
  input  _1B,
  input  _1C,
  input  _2A,
  input  _2B,
  input  _3C,
  input  _2C,
  input  _3B,
  input  _3A,
  input  GND,
  output _1Y,
  output _2Y,
  output _3Y
);

  nand nand_1 (_1Y, _1B, _1A, _1C);
  nand nand_2 (_2Y, _2C, _2B, _2A);
  nand nand_3 (_3Y, _3C, _3B, _3A);
endmodule

module _74HC153 (
  input  A,
  input  B,
  input  _1_nG,
  input  _1C0,
  input  _1C1,
  input  _1C2,
  input  _1C3,
  input  _2_nG,
  input  _2C0,
  input  _2C1,
  input  _2C2,
  input  _2C3,
  output _1Y,
  output _2Y
);

  MUX4to1 mux4to1_1 (.G(_1_nG), .A(A), .B(B), .D0(_1C0), .D1(_1C1), .D2(_1C2), .D3(_1C3), .Y(_1Y));
  MUX4to1 mux4to1_2 (.G(_2_nG), .A(A), .B(B), .D0(_2C0), .D1(_2C1), .D2(_2C2), .D3(_2C3), .Y(_2Y));
endmodule

// MUX
module MUX4to1 (
  input  G,
  input  A,
  input  B,
  input  D0,
  input  D1,
  input  D2,
  input  D3,
  output Y
);

  wire and_1_out, and_2_out, and_3_out, and_4_out, not_1_out, not_2_out, not_3_out;

  not not_1 (not_1_out, G);
  not not_2 (not_2_out, A);
  not not_3 (not_3_out, B);
  and and_1 (and_1_out, D0, not_2_out, not_3_out, not_1_out);
  and and_2 (and_2_out, D1, not_2_out, B, not_1_out);
  and and_3 (and_3_out, D2, A, not_3_out, not_1_out);
  and and_4 (and_4_out, D3, A, B, not_1_out);
  or or_1 (Y, and_1_out, and_2_out, and_3_out, and_4_out);
endmodule

module _74HC161 (
  input  nCLR,
  input  ENT,
  input  ENP,
  input  nLOAD,
  input  A,
  input  B,
  input  C,
  input  D,
  input  CK,
  input  in_10,
  input  in_11,
  output CO,
  output QA,
  output QB,
  output QC,
  output QD
);

  wire transistor_1_out, transistor_3_out, transistor_4_out, undriven;

  Transistor transistor_1 (.in(transistor_3_out), .out(transistor_1_out), .gate(in_11));
  Transistor transistor_2 (.in(transistor_3_out), .out(transistor_1_out), .gate(in_10));
  Transistor transistor_3 (.in(transistor_4_out), .out(transistor_3_out), .gate(in_10));
  Transistor transistor_4 (.in(1'b0), .out(transistor_4_out), .gate(undriven));
  // also tied to VCC on the sheet: transistor_1_out
endmodule

module HA (
  input  A,
  input  B,
  output S,
  output C
);

  xor xor_1 (S, A, B);
  and and_1 (C, A, B);
endmodule

module FA (
  input  Cin,
  input  A,
  input  B,
  output S,
  output C
);

  wire ha_1_c, ha_1_s, ha_2_c;

  HA ha_1 (.A(A), .B(B), .S(ha_1_s), .C(ha_1_c));
  HA ha_2 (.A(Cin), .B(ha_1_s), .S(S), .C(ha_2_c));
  or or_1 (C, ha_2_c, ha_1_c);
endmodule

// BFA
module _74HC283 (
  input  A1,
  input  A2,
  input  A3,
  input  A4,
  input  B1,
  input  B2,
  input  B3,
  input  B4,
  input  C0,
  output C4,
  output S4,
  output S3,
  output S2,
  output S1
);

  wire fa_2_c, fa_3_c, fa_4_c;

  FA fa_1 (.Cin(fa_2_c), .A(A4), .B(B4), .S(S4), .C(C4));
  FA fa_2 (.Cin(fa_3_c), .A(B3), .B(A3), .S(S3), .C(fa_2_c));
  FA fa_3 (.Cin(fa_4_c), .A(B2), .B(A2), .S(S2), .C(fa_3_c));
  FA fa_4 (.Cin(C0), .A(A1), .B(B1), .S(S1), .C(fa_4_c));
endmodule
